// Logisim project Digital Devices.circ as structural Verilog: 24 circuits, main circuit MUX_2
module MUX_2 (
  input  IN_0,
  input  IN_1,
  input  SEL,
  output OUT
);

  wire and_1_out, and_2_out, not_1_out;

  not not_1 (not_1_out, SEL);
  and and_1 (and_1_out, IN_0, not_1_out);
  and and_2 (and_2_out, IN_1, SEL);
  or or_1 (OUT, and_1_out, and_2_out);
endmodule

module MUX_4 (
  input  IN_0,
  input  IN_1,
  input  IN_2,
  input  IN_3,
  input  SEL_0,
  input  SEL_1,
  output OUT
);

  wire and_1_out, and_2_out, and_3_out, and_4_out, not_1_out, not_2_out;

  not not_1 (not_1_out, SEL_0);
  not not_2 (not_2_out, SEL_1);
  and and_1 (and_1_out, IN_0, not_1_out, not_2_out);
  and and_2 (and_2_out, IN_1, not_1_out, SEL_1);
  and and_3 (and_3_out, IN_2, SEL_0, not_2_out);
  and and_4 (and_4_out, IN_3, SEL_0, SEL_1);
  or or_1 (OUT, and_1_out, and_2_out, and_3_out, and_4_out);
endmodule

module MUX_8 (
  input  IN_0,
  input  IN_1,
  input  IN_2,
  input  IN_3,
  input  IN_4,
  input  IN_5,
  input  IN_6,
  input  IN_7,
  input  SEL_0,
  input  SEL_1,
  input  SEL_2,
  output OUT
);

  wire and_1_out, and_2_out, and_3_out, and_4_out, and_5_out, and_6_out, and_7_out, and_8_out, not_1_out,
       not_2_out, not_3_out;

  not not_1 (not_1_out, SEL_0);
  not not_2 (not_2_out, SEL_1);
  not not_3 (not_3_out, SEL_2);
  and and_1 (and_1_out, IN_0, not_1_out, not_2_out, not_3_out);
  and and_2 (and_2_out, IN_1, not_1_out, not_2_out, SEL_2);
  and and_3 (and_3_out, IN_2, not_1_out, SEL_1, not_3_out);
  and and_4 (and_4_out, IN_3, not_1_out, SEL_1, SEL_2);
  and and_5 (and_5_out, IN_4, SEL_0, not_2_out, not_3_out);
  and and_6 (and_6_out, IN_5, SEL_0, not_2_out, SEL_2);
  and and_7 (and_7_out, IN_6, SEL_0, SEL_1, not_3_out);
  and and_8 (and_8_out, IN_7, SEL_0, SEL_1, SEL_2);
  or or_1 (OUT, and_1_out, and_2_out, and_3_out, and_4_out, and_5_out, and_6_out, and_7_out, and_8_out);
endmodule

module DEMUX_2 (
  input  IN,
  input  SEL,
  output OUT_0,
  output OUT1
);

  wire not_1_out;

  not not_1 (not_1_out, SEL);
  and and_1 (OUT_0, IN, not_1_out);
  and and_2 (OUT1, IN, SEL);
endmodule

module DEMUX_4 (
  input  IN,
  input  SEL_0,
  input  SEL_1,
  output OUT_0,
  output OUT_1,
  output OUT_2,
  output OUT_3
);

  wire not_1_out, not_2_out;

  not not_1 (not_1_out, SEL_0);
  not not_2 (not_2_out, SEL_1);
  and and_1 (OUT_0, IN, not_1_out, not_2_out);
  and and_2 (OUT_1, IN, not_1_out, SEL_1);
  and and_3 (OUT_2, IN, SEL_0, not_2_out);
  and and_4 (OUT_3, IN, SEL_0, SEL_1);
endmodule

module DEMUX_8 (
  input  IN,
  input  SEL_0,
  input  SEL_1,
  input  SEL_2,
  output OUT_0,
  output OUT_1,
  output OUT_2,
  output OUT_3,
  output OUT_4,
  output OUT_5,
  output OUT_6,
  output OUT_7
);

  wire not_1_out, not_2_out, not_3_out;

  not not_1 (not_1_out, SEL_0);
  not not_2 (not_2_out, SEL_1);
  not not_3 (not_3_out, SEL_2);
  and and_1 (OUT_0, IN, not_1_out, not_2_out, not_3_out);
  and and_2 (OUT_1, IN, not_1_out, not_2_out, SEL_2);
  and and_3 (OUT_2, IN, not_1_out, SEL_1, not_3_out);
  and and_4 (OUT_3, IN, not_1_out, SEL_1, SEL_2);
  and and_5 (OUT_4, IN, SEL_0, not_2_out, not_3_out);
  and and_6 (OUT_5, IN, SEL_0, not_2_out, SEL_2);
  and and_7 (OUT_6, IN, SEL_0, SEL_1, not_3_out);
  and and_8 (OUT_7, IN, SEL_0, SEL_1, SEL_2);
endmodule

module DEC_2 (
  input  IN_0,
  output OUT_0,
  output OUT_1
);

  not not_1 (OUT_0, IN_0);

  assign OUT_1 = IN_0;
endmodule

module DEC_4 (
  input  IN_0,
  input  IN_1,
  output OUT_0,
  output OUT_1,
  output OUT_2,
  output OUT_3
);

  wire not_1_out, not_2_out;

  not not_1 (not_1_out, IN_0);
  not not_2 (not_2_out, IN_1);
  and and_1 (OUT_0, not_1_out, not_2_out);
  and and_2 (OUT_1, not_1_out, IN_1);
  and and_3 (OUT_2, IN_0, not_2_out);
  and and_4 (OUT_3, IN_0, IN_1);
endmodule

module DEC_8 (
  input  IN_0,
  input  IN_1,
  input  IN_2,
  output OUT_0,
  output OUT_1,
  output OUT_2,
  output OUT_3,
  output OUT_4,
  output OUT_5,
  output OUT_6,
  output OUT_7
);

  wire not_1_out, not_2_out, not_3_out;

  not not_1 (not_1_out, IN_0);
  not not_2 (not_2_out, IN_1);
  not not_3 (not_3_out, IN_2);
  and and_1 (OUT_0, not_1_out, not_2_out, not_3_out);
  and and_2 (OUT_1, not_1_out, not_2_out, IN_2);
  and and_3 (OUT_2, not_1_out, IN_1, not_3_out);
  and and_4 (OUT_3, not_1_out, IN_1, IN_2);
  and and_5 (OUT_4, IN_0, not_2_out, not_3_out);
  and and_6 (OUT_5, IN_0, not_2_out, IN_2);
  and and_7 (OUT_6, IN_0, IN_1, not_3_out);
  and and_8 (OUT_7, IN_0, IN_1, IN_2);
endmodule

module ENC_2 (
  input  IN_0,
  input  IN_1,
  output OUT_0
);


  assign OUT_0 = IN_1;
endmodule

module ENC_4 (
  input  IN_0,
  input  IN_1,
  input  IN_2,
  input  IN_3,
  output OUT_0,
  output OUT_1
);

  or or_1 (OUT_0, IN_3, IN_2);
  or or_2 (OUT_1, IN_3, IN_1);
endmodule

module ENC_8 (
  input  IN_0,
  input  IN_1,
  input  IN_2,
  input  IN_3,
  input  IN_4,
  input  IN_5,
  input  IN_6,
  input  IN_7,
  output OUT_0,
  output OUT_1,
  output OUT_2
);

  or or_1 (OUT_0, IN_7, IN_6, IN_5, IN_4);
  or or_2 (OUT_1, IN_7, IN_6, IN_3, IN_2);
  or or_3 (OUT_2, IN_7, IN_5, IN_3, IN_1);
endmodule

module HALF_ADD (
  input  A,
  input  B,
  output S,
  output C_OUT
);

  xor xor_1 (S, A, B);
  and and_1 (C_OUT, A, B);
endmodule

module FULL_ADD (
  input  C_IN,
  input  A,
  input  B,
  output S,
  output C_OUT
);

  wire and_1_out, and_2_out, xor_1_out;

  xor xor_1 (xor_1_out, A, B);
  xor xor_2 (S, C_IN, xor_1_out);
  and and_1 (and_1_out, C_IN, xor_1_out);
  and and_2 (and_2_out, A, B);
  or or_1 (C_OUT, and_1_out, and_2_out);
endmodule

module HALF_SUB (
  input  A,
  input  B,
  output S,
  output C_OUT
);

  wire not_1_out;

  not not_1 (not_1_out, A);
  xor xor_1 (S, A, B);
  and and_1 (C_OUT, not_1_out, B);
endmodule

module FULL_SUB (
  input  C_IN,
  input  A,
  input  B,
  output S,
  output C_OUT
);

  wire and_1_out, and_2_out, not_1_out, not_2_out, xor_1_out;

  xor xor_1 (xor_1_out, A, B);
  not not_1 (not_1_out, A);
  and and_1 (and_1_out, not_1_out, B);
  not not_2 (not_2_out, xor_1_out);
  xor xor_2 (S, C_IN, xor_1_out);
  and and_2 (and_2_out, not_2_out, C_IN);
  or or_1 (C_OUT, and_2_out, and_1_out);
endmodule

module MULT (
  input  A,
  input  B,
  output OUT
);

  and and_1 (OUT, A, B);
endmodule

module DIV (
  input  A,
  input  B,
  output OUT,
  output ERROR
);

  wire and_1_out, not_1_out, or_1_out;

  not not_1 (not_1_out, A);
  not not_2 (ERROR, B);
  or or_1 (or_1_out, A, not_1_out);
  and and_1 (and_1_out, or_1_out, B);
  and and_2 (OUT, and_1_out, A);
endmodule

module COMP (
  input  A,
  input  B,
  output LESS,
  output EQUAL,
  output MORE
);

  wire not_1_out, not_2_out, or_1_out;

  not not_1 (not_1_out, A);
  not not_2 (not_2_out, B);
  and and_1 (LESS, not_1_out, B);
  and and_2 (MORE, A, not_2_out);
  or or_1 (or_1_out, LESS, MORE);
  not not_3 (EQUAL, or_1_out);
endmodule

module SR_FF_ASYN (
  input  S,
  input  R,
  output Q,
  output nQ
);

  nor nor_1 (nQ, S, Q);
  nor nor_2 (Q, nQ, R);
endmodule

module SR_FF_SYN (
  input  S,
  input  CLK,
  input  R,
  output Q,
  output nQ
);

  wire nand_1_out, nand_2_out;

  nand nand_1 (nand_1_out, S, CLK);
  nand nand_2 (nand_2_out, CLK, R);
  nand nand_3 (Q, nand_1_out, nQ);
  nand nand_4 (nQ, Q, nand_2_out);
endmodule

module D_FF (
  input  D,
  input  CLK,
  output Q,
  output nQ
);

  wire nand_1_out, nand_2_out, not_1_out;

  not not_1 (not_1_out, D);
  nand nand_1 (nand_1_out, D, CLK);
  nand nand_2 (nand_2_out, not_1_out, CLK);
  nand nand_3 (Q, nand_1_out, nQ);
  nand nand_4 (nQ, Q, nand_2_out);
endmodule

module JK_FF (
  input  J,
  input  CLK,
  input  K,
  output Q,
  output nQ
);

  wire nand_1_out, nand_2_out;

  nand nand_1 (nand_1_out, J, CLK, nQ);
  nand nand_2 (nand_2_out, Q, CLK, K);
  nand nand_3 (Q, nand_1_out, nQ);
  nand nand_4 (nQ, Q, nand_2_out);
endmodule

module T_FF (
  input  T,
  input  CLK,
  output Q,
  output nQ
);

  wire nand_1_out, nand_2_out, nand_3_out, nand_4_out, nand_5_out, nand_6_out;

  nand nand_1 (nand_1_out, T, CLK, nQ);
  nand nand_2 (nand_2_out, Q, CLK, T);
  nand nand_3 (nand_3_out, nand_1_out, nand_4_out);
  nand nand_4 (nand_4_out, nand_3_out, nand_2_out);
  nand nand_5 (nand_5_out, nand_1_out, nand_3_out);
  nand nand_6 (nand_6_out, nand_4_out, nand_2_out);
  nand nand_7 (Q, nand_5_out, nQ);
  nand nand_8 (nQ, Q, nand_6_out);
endmodule
